// Digital circuit ALU.dig as structural Verilog
module ALU (
  input  [2:0] Select,
  input  [7:0] A,
  input  [7:0] B,
  output [7:0] S
);

  wire [7:0] and_1_out, multiplicador4bit_1_p9, or_1_out, shiftleft8bit_1_p13, shiftright8bit_1_p9,
       somador8bit_1_p17, subtrator8bit_1_p19, xor_1_out;

  // ShiftLeft8Bit shiftleft8bit_1: pin names not known; wires that end beside it: A[0], A[1], A[2], A[3], A[4], A[5], A[6], A[7], shiftleft8bit_1_p13[0], shiftleft8bit_1_p13[1], shiftleft8bit_1_p13[2], shiftleft8bit_1_p13[3], shiftleft8bit_1_p13[4], shiftleft8bit_1_p13[5], shiftleft8bit_1_p13[6], shiftleft8bit_1_p13[7]
  // ShiftRight8Bit shiftright8bit_1: pin names not known; wires that end beside it: A[0], A[1], A[2], A[3], A[4], A[5], A[6], A[7], shiftright8bit_1_p9[0], shiftright8bit_1_p9[1], shiftright8bit_1_p9[2], shiftright8bit_1_p9[3], shiftright8bit_1_p9[4], shiftright8bit_1_p9[5], shiftright8bit_1_p9[6], shiftright8bit_1_p9[7]
  // Multiplicador4Bit multiplicador4bit_1: pin names not known; wires that end beside it: B[0], B[1], B[2], B[3], A[0], A[1], A[2], A[3], multiplicador4bit_1_p9[0], multiplicador4bit_1_p9[1], multiplicador4bit_1_p9[2], multiplicador4bit_1_p9[3], multiplicador4bit_1_p9[4], multiplicador4bit_1_p9[5], multiplicador4bit_1_p9[6], multiplicador4bit_1_p9[7]
  // SOmador8Bit somador8bit_1: pin names not known; wires that end beside it: A[0], B[0], 1'b0, A[1], B[1], A[2], B[2], A[3], B[3], A[4], A[5], A[6], A[7], B[4], B[5], B[6], somador8bit_1_p17[0], somador8bit_1_p17[1], somador8bit_1_p17[2], somador8bit_1_p17[3], somador8bit_1_p17[4], somador8bit_1_p17[5], somador8bit_1_p17[6], somador8bit_1_p17[7]
  // Subtrator8Bit subtrator8bit_1: pin names not known; wires that end beside it: B[7], A[0], A[1], A[2], A[3], B[0], B[1], B[2], B[3], 1'b0, A[4], B[4], A[5], B[5], A[6], B[6], A[7], B[7], subtrator8bit_1_p19[0], subtrator8bit_1_p19[1], subtrator8bit_1_p19[2], subtrator8bit_1_p19[3], subtrator8bit_1_p19[4], subtrator8bit_1_p19[5], subtrator8bit_1_p19[6], subtrator8bit_1_p19[7]
  assign or_1_out = A | B;  // Or or_1, 8 bits wide
  assign xor_1_out = A ^ B;  // XOr xor_1, 8 bits wide
  assign and_1_out = A & B;  // And and_1, 8 bits wide
  Multiplexer #(.Selector_Bits(3), .Bits(8)) multiplexer_1 (
    .sel(Select), .in_0(shiftleft8bit_1_p13), .in_1(shiftright8bit_1_p9), .in_2(or_1_out), .in_3(xor_1_out),
    .in_4(and_1_out), .in_5(multiplicador4bit_1_p9), .in_6(somador8bit_1_p17), .in_7(subtrator8bit_1_p19),
    .out(S));

  // Other names for the same wires on the sheet: A1 = A[0]; A2 = A[1]; A3 = A[2]; A4 = A[3]; A5 = A[4]; A6 = A[5];
  //   A7 = A[6]; A8 = A[7]; B1 = B[0]; B2 = B[1]; B3 = B[2]; B4 = B[3]; B5 = B[4]; B6 = B[5]; B7 = B[6]; B8 = B[7]
endmodule
