// Digital circuit CPU.dig as structural Verilog
module CPU (
  input  [2:0] in_1
);

  wire button_1_out;
  wire [2:0] Select;
  wire [3:0] register_1_q, register_1_q_2;
  wire [7:0] alu_1_s, eepromdualport_1_d;

  Button button_1 (.out(button_1_out));
  EEPROMDualPort #(.AddrBits(3), .Bits(11)) eepromdualport_1 (
    .A(in_1), .Din({11{1'b0}}), .str(1'b0), .C(button_1_out), .ld(1'b1), .D({Select, eepromdualport_1_d}));
  ALU alu_1 (.Select(Select), .A(eepromdualport_1_d), .B({register_1_q_2, register_1_q}), .S(alu_1_s));
  Register #(.Bits(8)) register_1 (.D(alu_1_s), .C(button_1_out), .en(1'b1), .Q({register_1_q_2, register_1_q}));
  Seven_Seg_Hex seven_seg_hex_1 (.d(register_1_q_2), .dp(1'b0));
  Seven_Seg_Hex seven_seg_hex_2 (.d(register_1_q), .dp(1'b0));

  // Notes on the sheet:
  //   contents of eepromdualport_1 (hex, n*v repeats v):
  //   604,707,502
endmodule
